# Fritzing sketch Squeezebox (saved by Fritzing 0.9.2b)
breadboards: 1

parts:
  S1 = Pushbutton [package="[THT]"]
  Raspberry_Pi1 = Raspberry Pi 2
  R1 = Resistor [tolerance=±5% resistance=10k package=THT]
  S2 = Pushbutton [package="[THT]"]
  IR1 = TSOP312.., 314.. [package=THT]
  Q1 = NPN-Transistor [package="SOT-23 [SMD]"]
  R3 = Resistor [tolerance=±5% resistance=10k package=THT]
  LED1 = LED - 3mm [color="Red (633nm)" package="3 mm [THT]"]
  J1 = ATX24 Pin Power Supply Connector [package=atx24_right_angle]
  R2 = Resistor [tolerance=±5% resistance=10k package=THT]
  R4 = Resistor [tolerance=±5% resistance=10k package=THT]
  JP1 = USB_MICROB_PLUG [package=micro-b-th]

nets:
  N1: S1.Pin_1, S1.Pin_2, Raspberry_Pi1.GPIO5, R1.Pin_1
  GND: S1.Pin_3, S1.Pin_4, S2.Pin_3, S2.Pin_4, IR1.GND, Q1.2, J1.GND, R4.Pin_0, JP1.GND
  3V3: Raspberry_Pi1.3v3, Raspberry_Pi1.3V3, R1.Pin_0, IR1.Vs, R2.Pin_0
  N2: Raspberry_Pi1.GPIO4, R3.Pin_1
  N3: Raspberry_Pi1.GPIO22, IR1.Data
  N4: Raspberry_Pi1.GPIO6, S2.Pin_1, S2.Pin_2, R2.Pin_1
  N5: Q1.0, R3.Pin_0
  N6: Q1.1, J1.PS_ON
  N7: LED1.cathode, R4.Pin_1
  N8: LED1.anode, J1.3.3V
  N9: J1.5V_STDBY, JP1.VCC

notes:
  Power for the PI
